# Fritzing sketch UV_furnace_circuit (saved by Fritzing 0.9.2b)

parts:
  Bauteil1 = Arduino Mega 2560 (Rev3)
  THERMO1 = MAX31855 Breakout Board with Thermocouple
  Bauteil2 = Arduino Ethernet Shield (Rev3)
  LDD-1000H1 = MeanWell LDD-1000H
  KY-5 = Keyes Relay [package=THT]
  IC1 = DS3231MZ Real Time Clock
  U1 = Luxeon LED [package=luxeon]
  LDD-1000H2 = MeanWell LDD-1000H
  U2 = Luxeon LED [package=luxeon]
  LDD-1000H3 = MeanWell LDD-1000H
  U3 = Luxeon LED [package=luxeon]
  S1 = SWITCH-MOMENTARY-2 [package=reed_switch_pth]
  S2 = Square Pushbutton  # not connected
  R1 = Resistor [tolerance=±5% resistance=4.7k package="2010 [SMD]"]
  R2 = Resistor [tolerance=±5% resistance=4.7k package="2010 [SMD]"]
  R3 = Resistor [tolerance=±5% resistance=4.7k package="2010 [SMD]"]
  JACK1 = 2.1mm Barrel Jack with Terminal Block  # not connected
  C1 = Tantalum Capacitor [capacitance="1 μF" package="D 7343 [SMD, tantalum]"]
  LED1 = smd LED [color="Red (633nm)" package="0603 [SMD]"]

nets:
  N1: Bauteil1.D21/SCL, IC1.Pin_8
  N2: Bauteil1.D20/SDA, IC1.Pin_7
  N3: Bauteil1.D22, S1.2, C1.-
  N4: Bauteil1.D32, KY-5.ground
  N5: Bauteil1.D47, THERMO1.CS
  N6: Bauteil1.D50, THERMO1.DO
  N7: Bauteil1.D52, THERMO1.CLK
  VIN: THERMO1.Vin, Bauteil2.5V, KY-5.signal, IC1.Pin_2, S1.1, C1.+
  GND: THERMO1.GND, Bauteil2.GND, KY-5.power, IC1.Pin_5, R1.Pin_0, R2.Pin_0, R3.Pin_0
  N8: Bauteil2.SPI/D12, LED1.anode
  N9: Bauteil2.D2, IC1.Pin_3
  N10: Bauteil2.PWM_D5, LDD-1000H3.PWM_DIM, R3.Pin_1
  N11: Bauteil2.PWM_D6, LDD-1000H2.PWM_DIM, R2.Pin_1
  N12: Bauteil2.D7, LDD-1000H1.PWM_DIM, R1.Pin_1
  N13: LDD-1000H1.-Vin, U1.C
  N14: LDD-1000H1.+Vin, U1.A
  N15: LDD-1000H1.+Vout, LDD-1000H2.+Vout, LDD-1000H3.+Vout
  N16: LDD-1000H1.-Vout, LDD-1000H2.-Vout, LDD-1000H3.-Vout
  N17: LDD-1000H2.-Vin, U2.C
  N18: LDD-1000H2.+Vin, U2.A
  N19: LDD-1000H3.-Vin, U3.C
  N20: LDD-1000H3.+Vin, U3.A

notes:
  Nextion Display
  DS3231
  MAX31855
  Relay
  Meanwell LDD-500HW
  Heating Pad
  MEAN WELL RS-25-12
  IEC-Steckverbinder C14
  MEAN WELL PM-10-5
  prevents the LEDs from flashing when powering the Arduino on
  reed switch and 1 µF capacitor for hardware debouncing
  Rugged metal on/off switch with LED ring
  LED

custom parts:
  MeanWell LDD-1000H: DC-DC Constant Current Step-Down LED drive
  Keyes Relay: The Keyes 5V relay module is suitable for SCM development, home appliance control. It uses a 5V~12V TIL control signal which can control DC / AC signal.
  DS3231MZ Real Time Clock: DS3231MZ Real Time Clock. SO-8 surface mount version.
